# Fritzing sketch esquema (saved by Fritzing 0.9.3b)
breadboards: 1

parts:
  Part1 = Arduino Pro Mini (3.3V)
  CNY70-1 = CNY70 [package=cny70-side]
  LED1 = LED - 3mm [color="Red (633nm)" package="3 mm [THT]"]
  R1 = Resistor [tolerance=±5% resistance=120 package="0603 [SMD]"]
  VCC1 = 4 x AAA Battery Mount
  R2 = Resistor [tolerance=±5% resistance=10k package="0603 [SMD]"]
  R3 = Resistor [tolerance=±5% resistance=100 package="0603 [SMD]"]
  hc-sr1 = hc-sr04
  J1 = female pin header, 4 pins [form="♀ (female)"]  # not connected

nets:
  N1: Part1.RAW, VCC1.+, hc-sr1.VCC
  N2: Part1.GND, LED1.cathode, VCC1.-, R2.Pin_0
  N3: Part1.VCC, CNY70-1.E, R3.Pin_0
  N4: Part1.MISO, hc-sr1.Echo
  N5: Part1.MOSI, hc-sr1.Trig
  N6: Part1.D10, CNY70-1.C, R2.Pin_1
  N7: Part1.D9, CNY70-1.K
  N8: Part1.D8, hc-sr1.GND
  N9: Part1.D5, R1.Pin_1
  N10: CNY70-1.A, R3.Pin_1
  N11: LED1.anode, R1.Pin_0

custom parts:
  CNY70: PHOTOTRANSISTOR
